// Logisim project sim.circ as structural Verilog: 3 circuits, main circuit main
module main (
);

  wire A_OE, A_WE, ALU_A_WE, ALU_B_WE, ALU_OE, and_1_out, and_2_out, and_3_out, and_4_out, B_OE, B_WE, C_OE,
       C_WE, CLK, clock_1_out, CTRL_1_hlt, D_OE, D_WE, E_OE, E_WE, IR_WE, MAR2RAM, MAR_WE, MDR_DB, MDR_OE,
       MDR_WE, multiplexer_1_out, not_1_out, not_2_out, not_3_out, not_4_out, or_1_out, PC_INC, PC_OE, PC_WE,
       RAM_OE, RAM_WE;
  wire [2:0] STEPPER_q;
  wire [7:0] ALU_1_carry, register_1_q;
  wire [15:0] A_q, ALU_1_result, B_q, C_q, controlled_buffer_1_out, controlled_buffer_2_out, D_q, E_q, IR_q,
       MAR_q, MDR_q, PC_q, RAM_1_data;

  and and_1 (and_1_out, register_1_q[0], IR_q[7]);
  or or_1 (or_1_out, and_1_out, and_2_out, and_3_out, and_4_out);
  and and_2 (and_2_out, register_1_q[1], IR_q[6]);
  and and_3 (and_3_out, register_1_q[2], IR_q[5]);
  Counter #(.max('h7), .width(3)) STEPPER (
    .load(1'b0), .count(1'b1), .Q(STEPPER_q), .up(1'b1), .clk(not_1_out), .clr(or_1_out));  // open: D, carry
  not not_1 (not_1_out, CLK);
  and and_4 (and_4_out, register_1_q[3], IR_q[4]);
  RAM #(.addrWidth(16), .asyncread("true"), .dataWidth(16), .databus("bidir"), .\type ("nonvolatile")) RAM_1 (
    .addr(controlled_buffer_1_out), .we(RAM_WE), .oe(RAM_OE), .clk(CLK), .data(RAM_1_data));
  not not_2 (not_2_out, MAR2RAM);
  assign controlled_buffer_1_out = not_2_out ? PC_q : 16'bz;  // Controlled_Buffer controlled_buffer_1
  CTRL CTRL_1 (
    .STEP(STEPPER_q), .I(IR_q), .MAR2RAM(MAR2RAM), .MDR_OE(MDR_OE), .PC_OE(PC_OE), .MDR_WE(MDR_WE),
    .MAR_WE(MAR_WE), .A_OE(A_OE), .IR_WE(IR_WE), .B_OE(B_OE), .C_OE(C_OE), .D_OE(D_OE), .MDR_DB(MDR_DB),
    .RAM_WE(RAM_WE), .E_OE(E_OE), .RAM_OE(RAM_OE), .PC_INC(PC_INC), .ALU_A_WE(ALU_A_WE), .PC_WE(PC_WE),
    .ALU_B_WE(ALU_B_WE), .ALU_OE(ALU_OE), .HLT(CTRL_1_hlt), .A_WE(A_WE), .B_WE(B_WE), .C_WE(C_WE),
    .D_WE(D_WE), .E_WE(E_WE));
  not not_3 (not_3_out, CLK);
  Multiplexer multiplexer_1 (.in0(not_3_out), .in1(CLK), .out(multiplexer_1_out), .sel(PC_WE));
  Register #(.width(16)) IR (.D(RAM_1_data), .en(IR_WE), .clk(CLK), .Q(IR_q));  // open: clr
  Clock clock_1 (.out(clock_1_out));
  and and_5 (CLK, clock_1_out, not_4_out);
  not not_4 (not_4_out, CTRL_1_hlt);
  Counter #(.max('hffff), .width(16)) PC (
    .load(PC_WE), .D(controlled_buffer_2_out), .count(PC_INC), .Q(PC_q), .up(1'b1), .clk(multiplexer_1_out),
    .clr(1'b0));  // open: carry
  Register #(.width(16)) MAR (.D(controlled_buffer_2_out), .en(MAR_WE), .clk(CLK), .Q(MAR_q));  // open: clr
  Register #(.width(16)) MDR (.D(RAM_1_data), .en(MDR_WE), .clk(CLK), .Q(MDR_q));  // open: clr
  assign controlled_buffer_2_out = PC_OE ? PC_q : 16'bz;  // Controlled_Buffer controlled_buffer_2
  assign controlled_buffer_1_out = MAR2RAM ? MAR_q : 16'bz;  // Controlled_Buffer controlled_buffer_3
  assign RAM_1_data = MDR_DB ? controlled_buffer_2_out : 16'bz;  // Controlled_Buffer controlled_buffer_4
  assign controlled_buffer_2_out = MDR_OE ? MDR_q : 16'bz;  // Controlled_Buffer controlled_buffer_5
  Register #(.width(16)) A (.D(controlled_buffer_2_out), .en(A_WE), .clk(CLK), .Q(A_q));  // open: clr
  Register #(.width(16)) B (.D(controlled_buffer_2_out), .en(B_WE), .clk(CLK), .Q(B_q));  // open: clr
  Register #(.width(16)) C (.D(controlled_buffer_2_out), .en(C_WE), .clk(CLK), .Q(C_q));  // open: clr
  Register #(.width(16)) D (.D(controlled_buffer_2_out), .en(D_WE), .clk(CLK), .Q(D_q));  // open: clr
  Register #(.width(16)) E (.D(controlled_buffer_2_out), .en(E_WE), .clk(CLK), .Q(E_q));  // open: clr
  assign controlled_buffer_2_out = A_OE ? A_q : 16'bz;  // Controlled_Buffer controlled_buffer_6
  assign controlled_buffer_2_out = B_OE ? B_q : 16'bz;  // Controlled_Buffer controlled_buffer_7
  assign controlled_buffer_2_out = C_OE ? C_q : 16'bz;  // Controlled_Buffer controlled_buffer_8
  assign controlled_buffer_2_out = D_OE ? D_q : 16'bz;  // Controlled_Buffer controlled_buffer_9
  assign controlled_buffer_2_out = E_OE ? E_q : 16'bz;  // Controlled_Buffer controlled_buffer_10
  assign controlled_buffer_2_out = ALU_OE ? ALU_1_result : 16'bz;  // Controlled_Buffer controlled_buffer_11
  ALU ALU_1 (
    .A(controlled_buffer_2_out), .A_WE(ALU_A_WE), .B(controlled_buffer_2_out), .B_WE(ALU_B_WE), .CLK(CLK),
    .OP(IR_q[3:0]), .RESULT(ALU_1_result), .CARRY(ALU_1_carry[0]), .ZERO(ALU_1_carry[1]),
    .PARITY(ALU_1_carry[2]), .SIGN(ALU_1_carry[3]));
  Register register_1 (.D(ALU_1_carry), .en(ALU_OE), .clk(CLK), .Q(register_1_q));  // open: clr
endmodule

module ALU (
  input  [15:0] A,
  input  A_WE,
  input  [15:0] B,
  input  B_WE,
  input  CLK,
  input  [3:0] OP,
  output [15:0] RESULT,
  output CARRY,
  output ZERO,
  output PARITY,
  output SIGN
);

  wire and_2_out, not_1_out, not_2_out, not_3_out, or_2_out, xor_3_out, xor_4_out;
  wire [15:0] adder_1_out, and_1_out, bit_extender_1_out, multiplexer_1_out, multiplexer_2_out,
       multiplexer_3_out, multiplexer_4_out, or_1_out, register_1_q, register_2_q, shifter_1_out,
       shifter_2_out, xor_1_out, xor_2_out;

  Register #(.width(16)) register_1 (.D(A), .en(A_WE), .clk(CLK), .Q(register_1_q));  // open: clr
  Register #(.width(16)) register_2 (.D(B), .en(B_WE), .clk(CLK), .Q(register_2_q));  // open: clr
  not not_1 (not_1_out, OP[0]);
  assign bit_extender_1_out = {{15{not_1_out}}, not_1_out};  // Bit_Extender bit_extender_1
  assign xor_1_out = register_2_q ^ bit_extender_1_out;  // XOR_Gate xor_1, 16 bits wide
  assign or_1_out = register_1_q | register_2_q;  // OR_Gate or_1, 16 bits wide
  Multiplexer #(.width(16)) multiplexer_1 (.in0(or_1_out), .in1(and_1_out), .out(multiplexer_1_out), .sel(not_2_out));
  assign and_1_out = register_1_q & register_2_q;  // AND_Gate and_1, 16 bits wide
  not not_2 (not_2_out, OP[0]);
  assign xor_2_out = register_1_q ^ register_2_q;  // XOR_Gate xor_2, 16 bits wide
  Multiplexer #(.width(16)) multiplexer_2 (
    .in0(xor_2_out), .in1(shifter_1_out), .out(multiplexer_2_out), .sel(not_3_out));
  Shifter #(.width(16)) shifter_1 (.in(register_1_q), .\dist (register_2_q[3:0]), .out(shifter_1_out));
  not not_3 (not_3_out, OP[0]);
  Shifter #(.shift("lr"), .width(16)) shifter_2 (.in(register_1_q), .\dist (register_2_q[3:0]), .out(shifter_2_out));
  Adder #(.width(16)) adder_1 (.a(register_1_q), .b(xor_1_out), .out(adder_1_out), .cin(not_1_out), .cout(CARRY));
  xor xor_3 (xor_3_out, OP[0], OP[1]);
  xor xor_4 (xor_4_out, OP[0], OP[1]);
  Multiplexer #(.width(16)) multiplexer_3 (
    .in0(adder_1_out), .in1(multiplexer_1_out), .out(multiplexer_3_out), .sel(xor_3_out));
  Multiplexer #(.width(16)) multiplexer_4 (
    .in0(multiplexer_2_out), .in1(shifter_2_out), .out(multiplexer_4_out), .sel(xor_4_out));
  Multiplexer #(.width(16)) multiplexer_5 (
    .in0(multiplexer_3_out), .in1(multiplexer_4_out), .out(RESULT), .sel(or_2_out));
  or or_2 (or_2_out, and_2_out, OP[3]);
  and and_2 (and_2_out, OP[0], OP[1], OP[2]);
  nor nor_1 (ZERO, RESULT[0], RESULT[1], RESULT[2], RESULT[3], RESULT[4], RESULT[5], RESULT[6], RESULT[7], RESULT[8], RESULT[9], RESULT[10], RESULT[11], RESULT[12], RESULT[13], RESULT[14], RESULT[15]);

  assign PARITY = 1'b0;
  assign SIGN = RESULT[15];

  // Notes on the sheet:
  //   0011: A+B
  //   0100: A-B
  //   0101: A v B
  //   0110: A ^ B
  //   0111: A xor B
  //   1000: A << B
  //   1001: A >> B
endmodule

module CTRL (
  input  [2:0] STEP,
  input  [15:0] I,
  output MAR2RAM,
  output MDR_OE,
  output PC_OE,
  output MDR_WE,
  output MAR_WE,
  output A_OE,
  output IR_WE,
  output B_OE,
  output C_OE,
  output D_OE,
  output MDR_DB,
  output RAM_WE,
  output E_OE,
  output RAM_OE,
  output PC_INC,
  output ALU_A_WE,
  output PC_WE,
  output ALU_B_WE,
  output ALU_OE,
  output HLT,
  output A_WE,
  output B_WE,
  output C_WE,
  output D_WE,
  output E_WE
);

  wire demultiplexer_1_out0, demultiplexer_1_out1, demultiplexer_1_out2, demultiplexer_1_out3,
       demultiplexer_1_out4, demultiplexer_1_out5, demultiplexer_2_out0, demultiplexer_2_out1,
       demultiplexer_2_out2, demultiplexer_2_out3, demultiplexer_2_out4, demultiplexer_2_out5,
       demultiplexer_3_out0, demultiplexer_3_out1, demultiplexer_3_out2, demultiplexer_3_out3,
       demultiplexer_3_out4, demultiplexer_3_out5, demultiplexer_4_out0, demultiplexer_4_out1,
       demultiplexer_4_out2, demultiplexer_4_out3, demultiplexer_4_out4, demultiplexer_4_out5, or_6_out,
       or_13_out, or_15_out;
  wire [23:2] ROM_1_data;

  ROM #(.dataWidth(24)) ROM_1 (
    .addr({1'b0, I[3:0], STEP}),
    .data({ROM_1_data[23:20], HLT, ALU_OE, ALU_B_WE, ALU_A_WE, PC_INC, RAM_OE, RAM_WE, MDR_DB, ROM_1_data[11:7], IR_WE, ROM_1_data[5], MAR_WE, MDR_WE, ROM_1_data[2], MDR_OE, MAR2RAM}));
  Demultiplexer #(.select(3)) demultiplexer_1 (
    .out0(demultiplexer_1_out0), .out1(demultiplexer_1_out1), .out2(demultiplexer_1_out2),
    .out3(demultiplexer_1_out3), .out4(demultiplexer_1_out4), .out5(demultiplexer_1_out5),
    .in(ROM_1_data[7]), .sel(I[10:8]));  // open: out6, out7
  Demultiplexer #(.select(3)) demultiplexer_2 (
    .out0(demultiplexer_2_out0), .out1(demultiplexer_2_out1), .out2(demultiplexer_2_out2),
    .out3(demultiplexer_2_out3), .out4(demultiplexer_2_out4), .out5(demultiplexer_2_out5),
    .in(ROM_1_data[8]), .sel(I[14:12]));  // open: out6, out7
  Demultiplexer #(.select(3)) demultiplexer_3 (
    .out0(demultiplexer_3_out0), .out1(demultiplexer_3_out1), .out2(demultiplexer_3_out2),
    .out3(demultiplexer_3_out3), .out4(demultiplexer_3_out4), .out5(demultiplexer_3_out5),
    .in(ROM_1_data[9]), .sel(I[10:8]));  // open: out6, out7
  Demultiplexer #(.select(3)) demultiplexer_4 (
    .out0(demultiplexer_4_out0), .out1(demultiplexer_4_out1), .out2(demultiplexer_4_out2),
    .out3(demultiplexer_4_out3), .out4(demultiplexer_4_out4), .out5(demultiplexer_4_out5),
    .in(ROM_1_data[10]), .sel(I[14:12]));  // open: out6, out7
  or or_1 (A_OE, demultiplexer_1_out0, demultiplexer_2_out0);
  or or_2 (B_OE, demultiplexer_1_out1, demultiplexer_2_out1);
  or or_3 (C_OE, demultiplexer_1_out2, demultiplexer_2_out2);
  or or_4 (D_OE, demultiplexer_1_out3, demultiplexer_2_out3);
  or or_5 (E_OE, demultiplexer_1_out4, demultiplexer_2_out4);
  or or_6 (or_6_out, demultiplexer_3_out0, demultiplexer_4_out0);
  or or_7 (B_WE, demultiplexer_3_out1, demultiplexer_4_out1);
  or or_8 (C_WE, demultiplexer_3_out2, demultiplexer_4_out2);
  or or_9 (D_WE, demultiplexer_3_out3, demultiplexer_4_out3);
  or or_10 (E_WE, demultiplexer_3_out4, demultiplexer_4_out4);
  or or_11 (A_WE, ROM_1_data[11], or_6_out);
  or or_12 (PC_OE, ROM_1_data[2], or_13_out);
  or or_13 (or_13_out, demultiplexer_1_out5, demultiplexer_2_out5);
  or or_14 (PC_WE, ROM_1_data[5], or_15_out);
  or or_15 (or_15_out, demultiplexer_3_out5, demultiplexer_4_out5);

  // Notes on the sheet:
  //   contents of ROM_1 (hex, n*v repeats v):
  //   c044 7*0 c044 110 4009 202 4*0 c044 110 88 3003 4*0 c044 10080 20100 40800 4*0 c044 10080 20100
  //   40800 4*0 c044 10080 20100 40800 4*0 c044 10080 20100 40800 4*0 c044 10080 20100 40800 4*0 c044
  //   10080 20100 40800 4*0 c044 10080 20100 40800 4*0 c044 480 6*0 c044 4008 22 5*0 c044 4008 202 8000
  //   4*0 c044 7*0 c044 7*0 c044
endmodule
